# Fritzing sketch schema (saved by Fritzing 0.9.4)
breadboards: 1

parts:
  Pololu_A1 = Pololu A4988 [package=SO16]
  Part1 = Arduino Nano (Rev3.0)
  M1 = Stepper Motor - Bipolar

nets:
  N1: Pololu_A1.ENABLE, Part1.D6
  N2: Pololu_A1.RESET, Pololu_A1.SLEEP
  N3: Pololu_A1.STEP, Part1.D5
  N4: Pololu_A1.DIR, Part1.D4
  N5: Pololu_A1.GND#8, Part1.GND
  VDD: Pololu_A1.VDD, Part1.5V
  N6: Pololu_A1.1B, M1.D
  N7: Pololu_A1.1A, M1.B
  N8: Pololu_A1.2A, M1.C
  N9: Pololu_A1.2B, M1.A
  GND: Pololu_A1.GND#14
  6V: Pololu_A1.VMOT

notes:
  Motor Power 6V
