# Fritzing sketch schema_old (saved by Fritzing 0.9.4)
circuit board: 9.08516cm x 3.30499cm
breadboards: 1

parts:
  Arduino = Arduino Nano (Rev3.0)
  M1 = Stepper Motor - Bipolar
  A4988_A2 = Pololu A4988 [package=SO16]
  A4988_A1 = Pololu A4988 [package=SO16]
  M2 = Stepper Motor - Bipolar
  Power = Power plug
  S1 = Basic Servo

nets:
  GND: Arduino.GND, A4988_A2.GND, A4988_A1.GND, Power.GND, S1.gnd
  N1: Arduino.D3, S1.pulse
  N2: Arduino.D4, A4988_A1.DIR
  N3: Arduino.D5, A4988_A1.STEP
  N4: Arduino.D6, A4988_A1.ENABLE
  N5: Arduino.D7, A4988_A2.ENABLE
  N6: Arduino.D8, A4988_A2.STEP
  N7: Arduino.D9, A4988_A2.DIR
  6V: Arduino.VIN, A4988_A2.VMOT, A4988_A1.VMOT, Power.VCC
  VDD: Arduino.5V, A4988_A2.VDD, A4988_A1.VDD, S1.vcc
  N8: M1.A, A4988_A1.2B
  N9: M1.C, A4988_A1.2A
  N10: M1.B, A4988_A1.1A
  N11: M1.D, A4988_A1.1B
  N12: A4988_A2.RESET, A4988_A2.SLEEP
  N13: A4988_A2.1B, M2.D
  N14: A4988_A2.1A, M2.B
  N15: A4988_A2.2A, M2.C
  N16: A4988_A2.2B, M2.A
  N17: A4988_A1.RESET, A4988_A1.SLEEP

notes:
  Power 9V
